# Fritzing sketch esquematico (saved by Fritzing 0.9.3b)
breadboards: 1

parts:
  Heltec_New_WiFi_Kit_1 = Heltec New WiFi Kit 32 [part_number=ZC-47]
  RHT1 = Humidity and Temperature Sensor RHT03
  R1 = Photocell (LDR) [package=THT]
  R_LDR = Resistor [tolerance=±5% resistance=220 package=THT]
  R_DTH = Resistor [tolerance=±5% resistance=220 package=THT]
  DS1 = DS18B20 1-Wire Temperature Sensor [part_number=DS18B20]
  R_dallas = Resistor [tolerance=±5% resistance=220 package=THT]

nets:
  N1: Heltec_New_WiFi_Kit_1.pin_23, R1.pin_1, R_LDR.Pin_1
  VCC: Heltec_New_WiFi_Kit_1.pin_16, Heltec_New_WiFi_Kit_1.pin_20, Heltec_New_WiFi_Kit_1.pin_4, RHT1.Vcc, R1.pin_0, R_DTH.Pin_0, DS1.VDD, R_dallas.Pin_0
  N2: Heltec_New_WiFi_Kit_1.pin_18, Heltec_New_WiFi_Kit_1.pin_19, RHT1.GND_2, R_LDR.Pin_0, DS1.GND
  N3: Heltec_New_WiFi_Kit_1.pin_21, Heltec_New_WiFi_Kit_1.pin_15
  N4: Heltec_New_WiFi_Kit_1.pin_2, RHT1.Data-signal, R_DTH.Pin_1
  N5: Heltec_New_WiFi_Kit_1.pin_7, DS1.DQ, R_dallas.Pin_1
