# Fritzing sketch esquematico_final (saved by Fritzing 0.9.3b)
breadboards: 1

parts:
  Componente2 = BH1750
  M1 = gy-213V
  DS3 = DS18B20 1-Wire Temperature Sensor Probe Cable
  Capacitive_Soil_Moisture_Sensor1 = DFRobot Capacitive Soil Moisture Sensor V1.0 [part_number=SEN0193]
  Heltec_WiFi_LoRa_32_V1 = Heltec WiFi LoRa 32 V2 [part_number=HTIT-WB32LA]

nets:
  VCC: Componente2.VCC, M1.VIN, DS3.VDD, Capacitive_Soil_Moisture_Sensor1.VCC, Heltec_WiFi_LoRa_32_V1.pin_16, Heltec_WiFi_LoRa_32_V1.pin_17
  GND: Componente2.GND, Componente2.ADDR, M1.GND, DS3.GND, Capacitive_Soil_Moisture_Sensor1.GND, Heltec_WiFi_LoRa_32_V1.pin_18, Heltec_WiFi_LoRa_32_V1.pin_19
  N1: Componente2.SCL, M1.SCL, Heltec_WiFi_LoRa_32_V1.pin_27
  N2: Componente2.SDA, M1.SDA, Heltec_WiFi_LoRa_32_V1.pin_1
  N3: Heltec_WiFi_LoRa_32_V1.pin_21, Heltec_WiFi_LoRa_32_V1.pin_22

custom parts:
  BH1750: Light Sensor
  gy-213V: GY-213V-HDC1080 Low Power High Precision Humidity Temperature Sensor Module.
  DFRobot Capacitive Soil Moisture Sensor V1.0: DFRobot Capacitive Soil Moisture Sensor V1.0 This product measures soil moisture levels by capacitive sensing, rather than resistive sensing like other types of moisture sensor. It is made of a corrosion resistant material giving it a long service life. Insert it into soil and impress your friends with the real-time soil moisture data! The product includes an on-board voltage regulator which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
  Heltec WiFi LoRa 32 V2: Heltec WiFi LoRa 32 V2 WiFi LoRa 32 is a classic IoT dev-board designed & produced by Heltec Automation(TM). It’s a highly integrated product based on ESP32 + SX127x, it has Wi-Fi, BLE, LoRa functions, also Li-Po battery management system, 0.96″ OLED are also included. It’s the best choice for smart cities, smart farms, smart home, and IoT makers.
