# Fritzing sketch esquematico_mini (saved by Fritzing 0.9.3b)
breadboards: 1

parts:
  Heltec_New_WiFi_Kit_2 = Heltec New WiFi Kit 32 [part_number=ZC-47]
  RLDR = Resistor [tolerance=±5% resistance=220 package=THT]
  RDallas = Resistor [tolerance=±5% resistance=220 package=THT]
  RHT2 = Humidity and Temperature Sensor RHT03
  R5 = Photocell (LDR) [package=THT]
  DS2 = DS18B20 1-Wire Temperature Sensor [part_number=DS18B20]
  RDTH22 = Resistor [tolerance=±5% resistance=220 package=THT]

nets:
  N1: Heltec_New_WiFi_Kit_2.pin_23, RLDR.Pin_0, R5.pin_0
  VCC: Heltec_New_WiFi_Kit_2.pin_16, Heltec_New_WiFi_Kit_2.pin_20, RDallas.Pin_1, RHT2.Vcc, R5.pin_1, DS2.VDD, RDTH22.Pin_1
  N2: Heltec_New_WiFi_Kit_2.pin_18, Heltec_New_WiFi_Kit_2.pin_19, RLDR.Pin_1, RHT2.GND_2, DS2.GND
  N3: Heltec_New_WiFi_Kit_2.pin_21, Heltec_New_WiFi_Kit_2.pin_15
  N4: Heltec_New_WiFi_Kit_2.pin_2, RHT2.Data-signal, RDTH22.Pin_0
  N5: Heltec_New_WiFi_Kit_2.pin_7, RDallas.Pin_0, DS2.DQ
